// Digital circuit CPU.dig as structural Verilog
module CPU (
  input  [15:0] inM,
  input  [15:0] instruction,
  input  CLK,
  output [15:0] outM,
  output writeM,
  output [14:0] addressM,
  output [14:0] pc
);

  wire undriven;
  wire [15:0] mux16_1_out;

  Mux16 mux16_1 (.a(instruction), .sel(instruction[0]), .out(mux16_1_out));  // open: b
  Register register_1 (.in(mux16_1_out), .CLK(undriven));  // open: load, out

  // Notes on the sheet:
  //   CLK: Hz: 10
endmodule
