// Digital circuit sketch.dig as structural Verilog
module sketch (
  input  [15:0] a,
  input  [15:0] b,
  input  [15:0] c,
  input  [15:0] d,
  input  [2:0] sel,
  input  [15:0] e,
  input  [15:0] f,
  input  [15:0] g,
  input  [15:0] h,
  output [15:0] out
);

  Mux4Way16 mux4way16_1 ();  // open: a, b, c, d, sel, out
endmodule
